# Fritzing sketch hydrocontrol_v1.2 (saved by Fritzing 0.9.4)
stripboards: 1

parts:
  U1 = NodeMCU V1.0
  J_PH = male pin header, 3 pins [form="♂ (male)"]
  C1 = Ceramic Capacitor [capacitance=100nF package="100 mil [THT, multilayer]"]
  C2 = Ceramic Capacitor [capacitance=100nF package="100 mil [THT, multilayer]"]
  C3 = Electrolytic Capacitor [capacitance=0.22mF package="100 mil [THT, electrolytic]"]
  Pololu_A1 = Pololu A4988 [package=SO16]
  J2 = double row male pin header, 4 pins [form="♂ (male)"]
  J_TEMP = male pin header, 3 pins [form="♂ (male)"]
  S_CAL_LOW = Pushbutton [package="[THT]"]
  S_CAL_HIGH = Pushbutton [package="[THT]"]
  Power_plug1 = Power plug
  U2 = Voltage Regulator - 5V [package="TO220 [THT]"]
  R3 = Resistor [tolerance=±5% resistance=4.7k package=THT]
  R4 = Resistor [tolerance=±5% resistance=150 package=THT]
  R7 = Resistor [tolerance=±5% resistance=2.2k package=THT]
  R5 = Resistor [tolerance=±5% resistance=150 package=THT]
  R6 = Resistor [tolerance=±5% resistance=2.2k package=THT]
  R1 = Resistor [tolerance=±5% resistance=2.2k package=THT]
  R2 = Resistor [tolerance=±5% resistance=1k package=THT]
  Q1 = NPN-Transistor [package="TO92 [THT]"]
  R8 = Resistor [tolerance=±5% resistance=330 package=THT]
  J_LED = molex pin header, 3 pins [form=molex]
  R9 = Resistor [tolerance=±5% resistance=1.5k package=THT]
  J_FAN1 = molex pin header, 2 pins [form=molex]
  Q2 = Basic FET N-Channel [package="TO220 [THT]"]
  R10 = Resistor [tolerance=±5% resistance=330 package=THT]

nets (from the schematic view):
  N1: U1.D1, J_TEMP.pin2, R3.Pin_1
  N2: U1.D2, Pololu_A1.DIR
  N3: U1.D3, Pololu_A1.STEP
  N4: U1.D4, Pololu_A1.ENABLE
  3.3V: U1.3V3, J_TEMP.pin1, R3.Pin_0
  GND: U1.GND, J_PH.pin3, C1.1, C2.0, C3.-, Pololu_A1.GND, J_TEMP.pin3, S_CAL_LOW.Pin_3, S_CAL_LOW.Pin_4, S_CAL_HIGH.Pin_3, S_CAL_HIGH.Pin_4, Power_plug1.GND, U2.GND, R1.Pin_1, Q1.E, J_LED.pin3, Q2.source
  N5: U1.D5, R4.Pin_0
  N6: U1.D6, R5.Pin_0
  N7: U1.D7, R8.Pin_0
  N8: U1.D8, R10.Pin_0
  5V: U1.Vin, J_PH.pin1, C2.1, Pololu_A1.MS1, Pololu_A1.MS2, Pololu_A1.MS3, Pololu_A1.VDD, U2.output_voltage, R7.Pin_0, R6.Pin_0, J_LED.pin1, R9.Pin_1
  N9: U1.A0, R1.Pin_0, R2.Pin_1
  N10: J_PH.pin2, R2.Pin_0
  N11: C1.0, U2.input_voltage
  N12: C3.+, Power_plug1.VCC
  N13: Pololu_A1.RESET, Pololu_A1.SLEEP
  N14: Pololu_A1.1B, J2.pin4
  N15: Pololu_A1.1A, J2.pin3
  N16: Pololu_A1.2A, J2.pin2
  N17: Pololu_A1.2B, J2.pin1
  12V: Pololu_A1.VMOT, J_FAN1.pin1
  N18: S_CAL_LOW.Pin_1, S_CAL_LOW.Pin_2, R5.Pin_1, R6.Pin_1
  N19: S_CAL_HIGH.Pin_1, S_CAL_HIGH.Pin_2, R4.Pin_1, R7.Pin_1
  N20: Q1.B, R8.Pin_1
  N21: Q1.C, J_LED.pin2, R9.Pin_0
  N22: J_FAN1.pin2, Q2.drain

custom parts:
  NodeMCU V1.0: ESP8266 based NodeMCU
